# Fritzing sketch rotary-encoder (saved by Fritzing 0.9.4)
breadboards: 1

parts:
  RE1 = Rotary Encoder [package=THT]
  Part1 = Arduino Uno (Rev3)

nets:
  N1: RE1.EncoderPinA, Part1.D4
  N2: RE1.EncoderPinC, Part1.GND
  N3: RE1.EncoderPinB, Part1.D3_PWM
