# Fritzing sketch seven-seg-direct (saved by Fritzing 0.9.4)
circuit board: 3.96332cm x 3.94307cm
breadboards: 1

parts:
  R1 = Resistor [tolerance=±5% resistance=220 package=THT]
  R2 = Resistor [tolerance=±5% resistance=220 package=THT]
  R3 = Resistor [tolerance=±5% resistance=220 package=THT]
  R4 = Resistor [tolerance=±5% resistance=220 package=THT]
  R5 = Resistor [tolerance=±5% resistance=220 package=THT]
  R6 = Resistor [tolerance=±5% resistance=220 package=THT]
  R7 = Resistor [tolerance=±5% resistance=220 package=THT]
  R8 = Resistor [tolerance=±5% resistance=220 package=THT]
  7_Segment1 = 7 Segment Display
  J1 = female pin header, 9 pins [form="♀ (female)"]

nets:
  PB0: R1.Pin_0, J1.pin2
  N1: R1.Pin_1, 7_Segment1.Segment_A
  PB1: R2.Pin_0, J1.pin3
  N2: R2.Pin_1, 7_Segment1.Segment_B
  PB2: R3.Pin_0, J1.pin4
  N3: R3.Pin_1, 7_Segment1.Segment_C
  PB3: R4.Pin_0, J1.pin5
  N4: R4.Pin_1, 7_Segment1.Segment_D
  PB4: R5.Pin_0, J1.pin6
  N5: R5.Pin_1, 7_Segment1.Segment_E
  PC0: R6.Pin_0, J1.pin7
  N6: R6.Pin_1, 7_Segment1.Segment_F
  PC1: R7.Pin_0, J1.pin8
  N7: R7.Pin_1, 7_Segment1.Segment_G
  PC2: R8.Pin_0, J1.pin9
  N8: R8.Pin_1, 7_Segment1.Segment_DP
  VCC: 7_Segment1.common_anode, J1.pin1
